# Fritzing sketch step2 (saved by Fritzing 0.9.2b)
breadboards: 1

parts:
  Part1 = Arduino Leonardo (Rev3b)
  S1 = Pushbutton [package="[THT]"]
  R2 = Resistor [tolerance=±5% resistance=10k package=THT]
  R1 = Resistor [tolerance=±5% resistance=220 package="0402 [SMD]"]
  LED1 = LED - 5mm [color="Red (633nm)" package="5 mm [THT]"]

nets:
  N1: Part1.5V, S1.Pin_3, S1.Pin_4
  N2: Part1.GND, R2.Pin_0, LED1.cathode
  N3: Part1.D11_PWM, S1.Pin_1, S1.Pin_2, R2.Pin_1
  N4: Part1.D13_PWM, R1.Pin_1
  N5: R1.Pin_0, LED1.anode
