# Fritzing sketch step3 (saved by Fritzing 0.9.2b)
breadboards: 1

parts:
  Part1 = Arduino Leonardo (Rev3b)
  LED1 = LED - 5mm [color="Red (633nm)" package="5 mm [THT]"]
  R1 = Resistor [tolerance=±5% resistance=220 package="0402 [SMD]"]
  R9 = Rotary Potentiometer (Small) [maximum_resistance=100kΩ package=THT]

nets:
  N1: Part1.5V, R9.leg2
  N2: Part1.GND, LED1.cathode, R9.leg1
  N3: Part1.A0, R9.wiper
  N4: Part1.D13_PWM, R1.Pin_1
  N5: LED1.anode, R1.Pin_0
