# Fritzing sketch step4 (saved by Fritzing 0.9.2b)
breadboards: 1

parts:
  Part1 = Arduino Leonardo (Rev3b)
  LED1 = LED - 5mm [color="Red (633nm)" package="5 mm [THT]"]
  R1 = Resistor [tolerance=±5% resistance=330 package="0402 [SMD]"]
  R7 = Resistor [tolerance=±5% resistance=1M package=THT]
  R8 = Resistor [tolerance=±5% resistance=1k package=THT]
  U2 = TOUCH [package=touch1]

nets:
  N1: Part1.D2/SDA, R8.Pin_1
  N2: Part1.GND, LED1.cathode
  N3: Part1.D13_PWM, R1.Pin_1
  N4: LED1.anode, R1.Pin_0
  N5: R7.Pin_1, R8.Pin_0, U2.T1
