# Fritzing sketch step5 (saved by Fritzing 0.9.2b)
breadboards: 1

parts:
  Part1 = Arduino Leonardo (Rev3b)
  LED1 = LED - 5mm [color="Red (633nm)" package="5 mm [THT]"]
  R1 = Resistor [tolerance=±5% resistance=220 package="0402 [SMD]"]
  R7 = Resistor [tolerance=±5% resistance=1M package=THT]
  U2 = TOUCH [package=touch1]
  R8 = Resistor [tolerance=±5% resistance=1k package=THT]

nets:
  N1: Part1.D2/SDA, Part1.SDA, R8.Pin_1
  N2: Part1.D4/A6, R7.Pin_0
  N3: Part1.GND, LED1.cathode
  N4: Part1.D13_PWM, R1.Pin_1
  N5: LED1.anode, R1.Pin_0
  N6: R7.Pin_1, U2.T1, R8.Pin_0
