# Fritzing sketch step6 (saved by Fritzing 0.9.2b)
breadboards: 1

parts:
  Part1 = Arduino Leonardo (Rev3b)
  LED1 = LED - 5mm [color="Red (633nm)" package="5 mm [THT]"]
  R1 = Resistor [tolerance=±5% resistance=220 package="0402 [SMD]"]
  S1 = Pushbutton [package="[THT]"]
  R2 = Resistor [tolerance=±5% resistance=10k package=THT]
  R5 = Resistor [tolerance=±5% resistance=10k package=THT]
  R6 = Photocell (LDR) [package=THT]
  R7 = Resistor [tolerance=±5% resistance=1M package=THT]
  R8 = Resistor [tolerance=±5% resistance=1k package=THT]
  U2 = TOUCH [package=touch1]
  R9 = Rotary Potentiometer (Small) [maximum_resistance=100kΩ package=THT]

nets:
  N1: Part1.D2/SDA, R8.Pin_1
  N2: Part1.D4/A6, R7.Pin_0
  N3: Part1.5V, S1.Pin_3, S1.Pin_4, R6.pin_0, R9.leg2
  N4: Part1.GND, LED1.cathode, R2.Pin_0, R5.Pin_0, R9.leg1
  N5: Part1.A0, R9.wiper
  N6: Part1.A2, R5.Pin_1, R6.pin_1
  N7: Part1.D11_PWM, S1.Pin_1, S1.Pin_2, R2.Pin_1
  N8: Part1.D13_PWM, R1.Pin_1
  N9: LED1.anode, R1.Pin_0
  N10: R7.Pin_1, R8.Pin_0, U2.T1
